// Logisim project RiskVAlu.circ as structural Verilog: 2 circuits, main circuit main
module main (
  input  [31:0] B,
  input  [31:0] A,
  input  Binvert,
  input  [1:0] Opselect,
  input  in_5,
  output Is_Zero,
  output [31:0] Result,
  output [31:0] SLT,
  output C_flag
);

  wire alu_1bit_1_c_out, alu_1bit_2_c_out, alu_1bit_3_c_out, alu_1bit_4_c_out, alu_1bit_5_c_out,
       alu_1bit_6_c_out, alu_1bit_7_c_out, alu_1bit_8_c_out, alu_1bit_9_c_out, alu_1bit_10_c_out,
       alu_1bit_11_c_out, alu_1bit_12_c_out, alu_1bit_13_c_out, alu_1bit_14_c_out, alu_1bit_15_c_out,
       alu_1bit_16_c_out, alu_1bit_17_c_out, alu_1bit_18_c_out, alu_1bit_19_c_out, alu_1bit_20_c_out,
       alu_1bit_21_c_out, alu_1bit_22_c_out, alu_1bit_23_c_out, alu_1bit_24_c_out, alu_1bit_26_c_out,
       alu_1bit_27_c_out, alu_1bit_28_c_out, alu_1bit_29_c_out, alu_1bit_30_c_out, alu_1bit_31_c_out,
       alu_1bit_32_c_out;

  ALU_1bit alu_1bit_1 (
    .Binvert(A[30]), .A(A[0]), .B(B[0]), .CarryIn(A[30]), .OpCode(Opselect), .result(Result[0]),
    .C_out(alu_1bit_1_c_out));
  ALU_1bit alu_1bit_2 (
    .Binvert(A[30]), .A(A[1]), .B(B[1]), .CarryIn(alu_1bit_1_c_out), .OpCode(Opselect), .result(Result[1]),
    .C_out(alu_1bit_2_c_out));
  ALU_1bit alu_1bit_3 (
    .Binvert(A[30]), .A(A[2]), .B(B[2]), .CarryIn(alu_1bit_2_c_out), .OpCode(Opselect), .result(Result[2]),
    .C_out(alu_1bit_3_c_out));
  ALU_1bit alu_1bit_4 (
    .Binvert(A[30]), .A(A[3]), .B(B[3]), .CarryIn(alu_1bit_3_c_out), .OpCode(Opselect), .result(Result[3]),
    .C_out(alu_1bit_4_c_out));
  ALU_1bit alu_1bit_5 (
    .Binvert(A[30]), .A(A[4]), .B(B[4]), .CarryIn(alu_1bit_4_c_out), .OpCode(Opselect), .result(Result[4]),
    .C_out(alu_1bit_5_c_out));
  ALU_1bit alu_1bit_6 (
    .Binvert(A[30]), .A(A[5]), .B(B[5]), .CarryIn(alu_1bit_5_c_out), .OpCode(Opselect), .result(Result[5]),
    .C_out(alu_1bit_6_c_out));
  ALU_1bit alu_1bit_7 (
    .Binvert(A[30]), .A(A[6]), .B(B[6]), .CarryIn(alu_1bit_6_c_out), .OpCode(Opselect), .result(Result[6]),
    .C_out(alu_1bit_7_c_out));
  ALU_1bit alu_1bit_8 (
    .Binvert(A[30]), .A(A[7]), .B(B[7]), .CarryIn(alu_1bit_7_c_out), .OpCode(Opselect), .result(Result[7]),
    .C_out(alu_1bit_8_c_out));
  ALU_1bit alu_1bit_9 (
    .Binvert(A[30]), .A(A[16]), .B(B[16]), .CarryIn(alu_1bit_17_c_out), .OpCode(Opselect),
    .result(Result[16]), .C_out(alu_1bit_9_c_out));
  ALU_1bit alu_1bit_10 (
    .Binvert(A[30]), .A(A[17]), .B(B[17]), .CarryIn(alu_1bit_9_c_out), .OpCode(Opselect),
    .result(Result[17]), .C_out(alu_1bit_10_c_out));
  ALU_1bit alu_1bit_11 (
    .Binvert(A[30]), .A(A[18]), .B(B[18]), .CarryIn(alu_1bit_10_c_out), .OpCode(Opselect),
    .result(Result[18]), .C_out(alu_1bit_11_c_out));
  ALU_1bit alu_1bit_12 (
    .Binvert(A[30]), .A(A[19]), .B(B[19]), .CarryIn(alu_1bit_11_c_out), .OpCode(Opselect),
    .result(Result[19]), .C_out(alu_1bit_12_c_out));
  ALU_1bit alu_1bit_13 (
    .Binvert(A[30]), .A(A[20]), .B(B[20]), .CarryIn(alu_1bit_12_c_out), .OpCode(Opselect),
    .result(Result[20]), .C_out(alu_1bit_13_c_out));
  ALU_1bit alu_1bit_14 (
    .Binvert(A[30]), .A(A[21]), .B(B[21]), .CarryIn(alu_1bit_13_c_out), .OpCode(Opselect),
    .result(Result[21]), .C_out(alu_1bit_14_c_out));
  ALU_1bit alu_1bit_15 (
    .Binvert(A[30]), .A(A[22]), .B(B[22]), .CarryIn(alu_1bit_14_c_out), .OpCode(Opselect),
    .result(Result[22]), .C_out(alu_1bit_15_c_out));
  ALU_1bit alu_1bit_16 (
    .Binvert(A[30]), .A(A[23]), .B(B[23]), .CarryIn(alu_1bit_15_c_out), .OpCode(Opselect),
    .result(Result[23]), .C_out(alu_1bit_16_c_out));
  ALU_1bit alu_1bit_17 (
    .Binvert(A[30]), .A(A[15]), .B(B[15]), .CarryIn(alu_1bit_18_c_out), .OpCode(Opselect),
    .result(Result[15]), .C_out(alu_1bit_17_c_out));
  ALU_1bit alu_1bit_18 (
    .Binvert(A[30]), .A(A[14]), .B(B[14]), .CarryIn(alu_1bit_19_c_out), .OpCode(Opselect),
    .result(Result[14]), .C_out(alu_1bit_18_c_out));
  ALU_1bit alu_1bit_19 (
    .Binvert(A[30]), .A(A[13]), .B(B[13]), .CarryIn(alu_1bit_20_c_out), .OpCode(Opselect),
    .result(Result[13]), .C_out(alu_1bit_19_c_out));
  ALU_1bit alu_1bit_20 (
    .Binvert(A[30]), .A(A[12]), .B(B[12]), .CarryIn(alu_1bit_21_c_out), .OpCode(Opselect),
    .result(Result[12]), .C_out(alu_1bit_20_c_out));
  ALU_1bit alu_1bit_21 (
    .Binvert(A[30]), .A(A[11]), .B(B[11]), .CarryIn(alu_1bit_22_c_out), .OpCode(Opselect),
    .result(Result[11]), .C_out(alu_1bit_21_c_out));
  ALU_1bit alu_1bit_22 (
    .Binvert(A[30]), .A(A[10]), .B(B[10]), .CarryIn(alu_1bit_23_c_out), .OpCode(Opselect),
    .result(Result[10]), .C_out(alu_1bit_22_c_out));
  ALU_1bit alu_1bit_23 (
    .Binvert(A[30]), .A(A[9]), .B(B[9]), .CarryIn(alu_1bit_24_c_out), .OpCode(Opselect), .result(Result[9]),
    .C_out(alu_1bit_23_c_out));
  ALU_1bit alu_1bit_24 (
    .Binvert(A[30]), .A(A[8]), .B(B[8]), .CarryIn(alu_1bit_8_c_out), .OpCode(Opselect), .result(Result[8]),
    .C_out(alu_1bit_24_c_out));
  ALU_1bit alu_1bit_25 (
    .Binvert(A[30]), .A(A[31]), .B(B[31]), .CarryIn(alu_1bit_26_c_out), .OpCode(Opselect),
    .result(Result[31]), .C_out(C_flag));
  ALU_1bit alu_1bit_26 (
    .Binvert(A[30]), .A(A[30]), .B(B[30]), .CarryIn(alu_1bit_27_c_out), .OpCode(Opselect),
    .result(Result[30]), .C_out(alu_1bit_26_c_out));
  ALU_1bit alu_1bit_27 (
    .Binvert(A[30]), .A(A[29]), .B(B[29]), .CarryIn(alu_1bit_28_c_out), .OpCode(Opselect),
    .result(Result[29]), .C_out(alu_1bit_27_c_out));
  ALU_1bit alu_1bit_28 (
    .Binvert(A[30]), .A(A[28]), .B(B[28]), .CarryIn(alu_1bit_29_c_out), .OpCode(Opselect),
    .result(Result[28]), .C_out(alu_1bit_28_c_out));
  ALU_1bit alu_1bit_29 (
    .Binvert(A[30]), .A(A[27]), .B(B[27]), .CarryIn(alu_1bit_30_c_out), .OpCode(Opselect),
    .result(Result[27]), .C_out(alu_1bit_29_c_out));
  ALU_1bit alu_1bit_30 (
    .Binvert(A[30]), .A(A[26]), .B(B[26]), .CarryIn(alu_1bit_31_c_out), .OpCode(Opselect),
    .result(Result[26]), .C_out(alu_1bit_30_c_out));
  ALU_1bit alu_1bit_31 (
    .Binvert(A[30]), .A(A[25]), .B(B[25]), .CarryIn(alu_1bit_32_c_out), .OpCode(Opselect),
    .result(Result[25]), .C_out(alu_1bit_31_c_out));
  ALU_1bit alu_1bit_32 (
    .Binvert(A[30]), .A(A[24]), .B(B[24]), .CarryIn(alu_1bit_16_c_out), .OpCode(Opselect),
    .result(Result[24]), .C_out(alu_1bit_32_c_out));
  nor nor_1 (Is_Zero, Result[0], Result[1], Result[2], Result[3], Result[4], Result[5], Result[6], Result[7], Result[8], Result[9], Result[10], Result[11], Result[12], Result[13], Result[14], Result[15], Result[16], Result[17], Result[18], Result[19], Result[20], Result[21], Result[22], Result[23], Result[24], Result[25], Result[26], Result[27], Result[28], Result[29], Result[30], Result[31]);

  assign Binvert = A[30];
  assign SLT = {{31{in_5}}, Result[31]};

  // Other names for the same wires on the sheet: sub = A[30]; op[1:0] = Opselect
endmodule

module ALU_1bit (
  input  Binvert,
  input  A,
  input  B,
  input  CarryIn,
  input  [1:0] OpCode,
  output result,
  output C_out
);

  wire adder_1_out, and_1_out, or_1_out, xor_1_out, xor_2_out;

  xor xor_1 (xor_1_out, Binvert, B);
  and and_1 (and_1_out, A, B);
  or or_1 (or_1_out, A, B);
  Adder #(.width(1)) adder_1 (.a(A), .b(xor_1_out), .out(adder_1_out), .cin(CarryIn), .cout(C_out));
  xor xor_2 (xor_2_out, A, B);
  Multiplexer #(.select(2)) multiplexer_1 (
    .in0(and_1_out), .in1(or_1_out), .in2(adder_1_out), .in3(xor_2_out), .out(result), .sel(OpCode));
endmodule
